# Fritzing sketch Wiring (saved by Fritzing 0.9.3b)
breadboards: 1

parts:
  hc-sr1 = hc-sr04
  S1 = Pushbutton [package="[SMD]"]
  LED1 = LED - 3mm [color="Red (633nm)" package="3 mm [THT]"]
  LED2 = LED - 3mm [color="Yellow (595nm)" package="3 mm [THT]"]
  LED3 = LED - 3mm [color="Green (555nm)" package="3 mm [THT]"]
  Part1 = Arduino Uno (Rev3)
  R1 = Resistor [tolerance=±5% resistance=1k package="0805 [SMD]"]
  R2 = Resistor [tolerance=±5% resistance=1k package="0805 [SMD]"]
  R3 = Resistor [tolerance=±5% resistance=1k package="0805 [SMD]"]
  R4 = Resistor [tolerance=±5% resistance=220 package="0805 [SMD]"]

nets:
  VCC: hc-sr1.VCC, S1.Pin_3, S1.Pin_4, Part1.5V
  N1: hc-sr1.Trig, Part1.D9_PWM
  N2: hc-sr1.Echo, Part1.D8
  GND: hc-sr1.GND, Part1.GND, R1.Pin_0, R2.Pin_0, R3.Pin_0, R4.Pin_0
  N3: S1.Pin_1, S1.Pin_2, Part1.D10_PWM/SS, R4.Pin_1
  N4: LED1.cathode, R3.Pin_1
  N5: LED1.anode, Part1.D5_PWM
  N6: LED2.cathode, R2.Pin_1
  N7: LED2.anode, Part1.D6_PWM
  N8: LED3.cathode, R1.Pin_1
  N9: LED3.anode, Part1.D7
